# Fritzing sketch Cyclone_Game_v3.1_Wiring_Schematics (saved by Fritzing 0.9.3b)

parts:
  25v_1000uf = Capacitor Polarized [package=panasonic_e]
  TM1637 = Grove 4 Digit Display
  Difficulty = Round Pushbutton
  Hit = Round Pushbutton
  Buzzer = Buzzer 12mm [package=buzzer-12mm-ns]
  RGB = WS2812 RGB LED strip
  Cyclone_Game_v3_1 = Arduino Nano (Rev3.0)
  part = Resistor [tolerance=±5% resistance=220 package="0402 [SMD]"]

nets:
  VCC: 25v_1000uf.+, TM1637.VCC, RGB.VCC, Cyclone_Game_v3_1.VIN
  GND: 25v_1000uf.-, TM1637.GND, Difficulty.leg0, Hit.leg0, Buzzer.2, RGB.GND, Cyclone_Game_v3_1.GND
  N1: TM1637.DIO, Cyclone_Game_v3_1.D10
  N2: TM1637.CLK, Cyclone_Game_v3_1.D9
  N3: Difficulty.leg1, Cyclone_Game_v3_1.D12/MISO
  N4: Hit.leg1, Cyclone_Game_v3_1.D11/MOSI
  N5: Buzzer.1, Cyclone_Game_v3_1.D3
  N6: RGB.DIN, part.Pin_0
  N7: Cyclone_Game_v3_1.D13/SCK, part.Pin_1

custom parts:
  WS2812 RGB LED strip: WS2812 strip
